// Digital circuit Bus Controller.dig as structural Verilog
module Bus_Controller (
  input  [15:0] Adr,
  input  BusEn,
  output Rom,
  output HRam,
  output Dev,
  output LRam
);

  wire and_1_out, and_2_out, comparator_1_eq, comparator_1_gt, comparator_1_lt, comparator_2_eq,
       comparator_2_gt, comparator_2_lt, comparator_3_eq, comparator_3_gt, comparator_3_lt, or_1_out,
       or_2_out, or_3_out;

  Comparator #(.Bits(16)) comparator_1 (
    .a(16'h4000), .b(Adr), .gt(comparator_1_gt), .eq(comparator_1_eq), .lt(comparator_1_lt));
  Comparator #(.Bits(16)) comparator_2 (
    .a(16'h8000), .b(Adr), .gt(comparator_2_gt), .eq(comparator_2_eq), .lt(comparator_2_lt));
  Comparator #(.Bits(16)) comparator_3 (
    .a(16'hfff0), .b(Adr), .gt(comparator_3_gt), .eq(comparator_3_eq), .lt(comparator_3_lt));
  or or_1 (or_1_out, comparator_1_eq, comparator_1_lt);
  or or_2 (or_2_out, comparator_2_eq, comparator_2_lt);
  or or_3 (or_3_out, comparator_3_eq, comparator_3_lt);
  and and_1 (and_1_out, or_1_out, comparator_2_gt);
  and and_2 (and_2_out, or_2_out, comparator_3_gt);
  and and_3 (Rom, comparator_1_gt, BusEn);
  and and_4 (LRam, and_1_out, BusEn);
  and and_5 (HRam, and_2_out, BusEn);
  and and_6 (Dev, or_3_out, BusEn);

  // Notes on the sheet:
  //   Adr: Adress cpu side
  //   Rom: rom enable
  //   HRam: ram enable
  //   LRam: ram enable
endmodule

/* Test case:
Adr	BusEn	Rom	LRam	HRam	Dev
0x0000	0	0	0	0	0
0x0000	1	1	0	0	0
0x3999	0	0	0	0	0
0x3999	1	1	0	0	0
0x4000	1	0	1	0	0
0x8000	1	0	0	1	0
0xFFF0	1	0	0	0	1
0xFFFF	1	0	0	0	1
0xFFFF	0	0	0	0	0
*/
