// Digital circuit device controller.dig as structural Verilog
module device_controller (
  input  [3:0] Adr,
  input  DevEn,
  input  W_nR,
  input  [7:0] DKeyb,
  output [7:0] D,
  output KeybEn,
  output [7:0] DTerm,
  output TermEn
);

  wire decoder_1_out_0, decoder_1_out_1;

  Decoder #(.Selector_Bits(4)) decoder_1 (
    .sel(Adr), .out_0(decoder_1_out_0), .out_1(decoder_1_out_1));  // open: out_2, out_3, out_4, out_5, out_6, out_7, out_8, out_9, out_10, out_11, out_12, out_13, out_14, out_15
  and and_1 (KeybEn, decoder_1_out_1, ~W_nR, DevEn);  // And
  and and_2 (TermEn, decoder_1_out_0, W_nR, DevEn);
  assign D = KeybEn ? DKeyb : 8'bz;  // Driver driver_1
  assign DTerm = TermEn ? D : 8'bz;  // Driver driver_2
endmodule

/* Test case:
D	Adr	DevEn	W/~R	DKeyb	KeybEn	DTerm	TermEn
Z	0x0	0	0	Z	0	Z	0
Z	0x0	1	0	Z	0	Z	0
Z	0x0	1	1	Z	0	x	1
Z	0x1	1	1	Z	0	Z	0
0x55	0x1	1	0	0x55	1	Z	0
*/
