// Digital circuit decoder test.dig as structural Verilog
module decoder_test (
  input  Flag,
  input  [3:0] Instruction,
  input  clk,
  input  Flag2
);

  wire and_1_out, and_2_out, and_3_out, and_4_out, demultiplexer_1_out_0, demultiplexer_1_out_1,
       demultiplexer_2_out_0, demultiplexer_2_out_1, Flag2Test, FlagTest, IR2Mc, IRLoad, LatchSelect,
       or_1_out, R, rs_ff_1_q, rs_ff_2_q, S, t_ff_1_nq, t_ff_1_q, TFet_Exec;
  wire [3:0] IR_q, NextMc;
  wire [7:0] MC_Addr_q, multiplexer_1_out, multiplexer_2_out, multiplexer_3_out;
  wire [15:0] Fetch_Code_d, MicroCode_d;

  Register #(.Bits(4)) IR (.D(Instruction), .C(clk), .en(IRLoad), .Q(IR_q));
  // Probe on IR_q
  T_FF t_ff_1 (.T(TFet_Exec), .C(clk), .Q(t_ff_1_q), .nQ(t_ff_1_nq));
  and and_1 (and_1_out, Flag, FlagTest);
  and and_2 (and_2_out, Flag2, Flag2Test);
  and and_3 (and_3_out, IR2Mc, t_ff_1_nq);
  or or_1 (or_1_out, and_1_out, and_2_out);
  Multiplexer #(.Bits(8)) multiplexer_1 (
    .sel(and_3_out), .in_0({MC_Addr_q[7:4], NextMc}), .in_1({IR_q, 4'b0000}), .out(multiplexer_1_out));
  and and_4 (and_4_out, TFet_Exec, t_ff_1_q);
  Multiplexer #(.Bits(8)) multiplexer_2 (
    .sel(and_4_out), .in_0(multiplexer_1_out), .in_1({4'b0000, NextMc}), .out(multiplexer_2_out));
  // Probe on multiplexer_2_out
  Demultiplexer demultiplexer_1 (
    .sel(LatchSelect), .in(S), .out_0(demultiplexer_1_out_0), .out_1(demultiplexer_1_out_1));
  Demultiplexer demultiplexer_2 (
    .sel(LatchSelect), .in(R), .out_0(demultiplexer_2_out_0), .out_1(demultiplexer_2_out_1));
  Register #(.Bits(8)) MC_Addr (.D(multiplexer_2_out), .C(clk), .en(1'b1), .Q(MC_Addr_q));
  // Probe on MC_Addr_q
  RS_FF rs_ff_1 (.S(demultiplexer_1_out_0), .C(clk), .R(demultiplexer_2_out_0), .Q(rs_ff_1_q));  // open: nQ
  RS_FF rs_ff_2 (.S(demultiplexer_1_out_1), .C(clk), .R(demultiplexer_2_out_1), .Q(rs_ff_2_q));  // open: nQ
  ROM #(.AddrBits(8), .Bits(16)) MicroCode (.A(MC_Addr_q), .sel(1'b1), .D(MicroCode_d));
  ROM #(.AddrBits(8), .Bits(16)) Fetch_Code (.A(MC_Addr_q), .sel(1'b1), .D(Fetch_Code_d));
  LED led_1 (.in(rs_ff_1_q));
  LED led_2 (.in(rs_ff_2_q));
  Multiplexer #(.Bits(16)) multiplexer_3 (
    .sel(t_ff_1_nq), .in_0(MicroCode_d), .in_1(Fetch_Code_d),
    .out({IRLoad, LatchSelect, FlagTest, Flag2Test, TFet_Exec, IR2Mc, R, S, multiplexer_3_out}));
  Multiplexer #(.Bits(4)) multiplexer_4 (
    .sel(or_1_out), .in_0(multiplexer_3_out[3:0]), .in_1(multiplexer_3_out[7:4]), .out(NextMc));
  // Probe on NextMc

  // Notes on the sheet:
  //   clk: Hz: 100
  //   contents of MicroCode (hex, n*v repeats v):
  //   a11,0,0,0,0,0,0,0,0,0,0,0,0,0,0,0,911,0,0,0,0,0,0,0,0,0,0,0,0,0,0,0,2081,4922,0,0,
  //   0,0,0,0,4a99,0,0,0,0,0,0,0,2018,4922,0,0,0,0,0,0,4a99,0,0,0,0,0,0,0,2012,5134,5234,
  //   900,a00
  //   contents of Fetch_Code (hex, n*v repeats v):
  //   8c00
endmodule
