// Digital circuit scpu test.dig as structural Verilog
module scpu_test (
  input  clk,
  input  in_2
);

  wire and_1_out, scpu_1_ben, scpu_1_w_nr;
  wire [7:0] scpu_1_d;
  wire [15:0] scpu_1_a;

  scpu scpu_1 (.clk(clk), .R(in_2), .D(scpu_1_d), .A(scpu_1_a), .W_nR(scpu_1_w_nr), .BEn(scpu_1_ben));
  // Probe DBus on scpu_1_d
  // Probe ABus on scpu_1_a
  and and_1 (and_1_out, clk, scpu_1_w_nr);
  EEPROM #(.AddrBits(16), .Bits(8)) eeprom_1 (
    .A(scpu_1_a), .CS(scpu_1_ben), .WE(and_1_out), .OE(~scpu_1_w_nr), .D(scpu_1_d));

  // Other names for the same wires on the sheet: r = in_2

  // Notes on the sheet:
  //   clk: Hz: 2147483647
  //   contents of eeprom_1 (hex, n*v repeats v):
  //   3,40,0,9,ff,f1,b,a,0,3,2,ff,f0,5,4,6,0,3
endmodule
