// Digital circuit scpu.dig as structural Verilog
module scpu (
  input  clk,
  input  R,
  output [7:0] D,
  output [15:0] A,
  output W_nR,
  output BEn
);

  simple_cpu simple_cpu_1 (
    .DMAreq(1'b0), .Nmi(1'b0), .Int(1'b0), .R(R), .Clk(clk), .D(D), .Adr(A), .W_nR(W_nR), .BEn(BEn));  // open: DMAack, Sync, IntAck

  // Notes on the sheet:
  //   clk: Hz: 2147483647
endmodule
