// Digital circuit simple pc.dig as structural Verilog
module simple_pc (
  input  clk
);

  wire and_1_out, and_2_out, and_3_out, and_4_out, bus_controller_1_dev, bus_controller_1_hram,
       bus_controller_1_lram, bus_controller_1_rom, device_controller_1_keyben, device_controller_1_termen,
       not_1_out, not_2_out, res, Reset_out, simple_cpu_1_ben, simple_cpu_1_dmaack, simple_cpu_1_intack,
       simple_cpu_1_sync, simple_cpu_1_w_nr;
  wire [7:0] device_controller_1_dterm, keyboard_1_d, simple_cpu_1_d;
  wire [13:0] simple_cpu_1_adr;
  wire [15:8] keyboard_1_d_2;
  wire [15:14] simple_cpu_1_adr_2;

  Button Reset (.out(Reset_out));
  Monoflop #(.timerDelay(16)) monoflop_1 (.C(Reset_out), .R(1'b0), .Q(res));  // open: nQ
  simple_cpu simple_cpu_1 (
    .DMAreq(1'b0), .Nmi(1'b0), .Int(1'b0), .R(res), .Clk(clk), .D(simple_cpu_1_d),
    .Adr({simple_cpu_1_adr_2, simple_cpu_1_adr}), .DMAack(simple_cpu_1_dmaack), .Sync(simple_cpu_1_sync),
    .W_nR(simple_cpu_1_w_nr), .BEn(simple_cpu_1_ben), .IntAck(simple_cpu_1_intack));
  LED led_1 (.in(simple_cpu_1_sync));
  LED led_2 (.in(simple_cpu_1_intack));
  LED led_3 (.in(simple_cpu_1_dmaack));
  Bus_Controller bus_controller_1 (
    .Adr({simple_cpu_1_adr_2, simple_cpu_1_adr}), .BusEn(simple_cpu_1_ben), .Rom(bus_controller_1_rom),
    .LRam(bus_controller_1_lram), .HRam(bus_controller_1_hram), .Dev(bus_controller_1_dev));
  ROM #(.AddrBits(14), .isProgramMemory("true"), .Bits(8)) rom_1 (
    .A(simple_cpu_1_adr), .sel(bus_controller_1_rom), .D(simple_cpu_1_d));
  // Probe Address on {simple_cpu_1_adr_2, simple_cpu_1_adr}
  // Probe Data on simple_cpu_1_d
  not not_1 (not_1_out, simple_cpu_1_w_nr);
  not not_2 (not_2_out, simple_cpu_1_w_nr);
  and and_1 (and_1_out, simple_cpu_1_w_nr, bus_controller_1_lram);
  and and_2 (and_2_out, not_1_out, bus_controller_1_lram);
  and and_3 (and_3_out, simple_cpu_1_w_nr, bus_controller_1_hram);
  and and_4 (and_4_out, not_2_out, bus_controller_1_hram);
  RAMSinglePort #(.AddrBits(14), .Bits(8)) ramsingleport_1 (
    .A(simple_cpu_1_adr), .str(and_1_out), .C(clk), .ld(and_2_out), .D(simple_cpu_1_d));
  RAMSinglePort #(.AddrBits(15), .Bits(8)) ramsingleport_2 (
    .A({simple_cpu_1_adr_2[14], simple_cpu_1_adr}), .str(and_3_out), .C(clk), .ld(and_4_out),
    .D(simple_cpu_1_d));
  device_controller device_controller_1 (
    .D(simple_cpu_1_d), .Adr(simple_cpu_1_adr[3:0]), .DevEn(bus_controller_1_dev), .W_nR(simple_cpu_1_w_nr),
    .DKeyb(keyboard_1_d), .KeybEn(device_controller_1_keyben), .DTerm(device_controller_1_dterm),
    .TermEn(device_controller_1_termen));
  Keyboard keyboard_1 (.C(clk), .en(device_controller_1_keyben), .D({keyboard_1_d_2, keyboard_1_d}));  // open: av
  Terminal #(.termWidth(40)) terminal_1 (.D(device_controller_1_dterm), .C(clk), .en(device_controller_1_termen));

  // Notes on the sheet:
  //   clk: Hz: 2147483647
  //   contents of rom_1 (hex, n*v repeats v):
  //   3,40,0,9,ff,f1,b,a,0,3,2,ff,f0,5,4,6,0,3
endmodule
